// Digital circuit 02-03.dig as structural Verilog
module _02_03 (
  input  A,
  input  B,
  input  Cin,
  output Problem_03__Sum,
  output Problem_03__Cout,
  output Problem_04__Sum,
  output Problem_04__Cout
);

  wire and_1_out, and_2_out, and_3_out, and_4_out, and_5_out, and_6_out, and_7_out, not_1_out, not_2_out,
       not_3_out, or_1_out, or_2_out, or_3_out, or_4_out, or_5_out, or_6_out, or_7_out;

  not not_1 (not_1_out, A);
  not not_2 (not_2_out, B);
  not not_3 (not_3_out, Cin);
  and and_1 (and_1_out, not_1_out, not_2_out, Cin);
  and and_2 (and_2_out, not_1_out, B, not_3_out);
  and and_3 (and_3_out, A, B, Cin);
  and and_4 (and_4_out, A, not_2_out, not_3_out);
  and and_5 (and_5_out, A, B);
  and and_6 (and_6_out, A, Cin);
  and and_7 (and_7_out, B, Cin);
  or or_1 (or_1_out, A, B, Cin);
  or or_2 (or_2_out, A, not_2_out, not_3_out);
  or or_3 (or_3_out, not_1_out, not_2_out, Cin);
  or or_4 (or_4_out, not_1_out, B, not_3_out);
  or or_5 (or_5_out, A, B);
  or or_6 (or_6_out, A, Cin);
  or or_7 (or_7_out, not_1_out, B, Cin);
  or or_8 (Problem_03__Sum, and_1_out, and_2_out, and_3_out, and_4_out);
  or or_9 (Problem_03__Cout, and_5_out, and_6_out, and_7_out);
  and and_8 (Problem_04__Sum, or_1_out, or_2_out, or_3_out, or_4_out);
  and and_9 (Problem_04__Cout, or_5_out, or_6_out, or_7_out);
endmodule
