// Digital circuit 02-07.dig as structural Verilog
module _02_07 (
  input  X0,
  input  X1,
  input  S,
  output Problem_7__Z__eq__m,
  output Problem_8__Z__eq__M
);

  wire and_1_out, and_2_out, not_1_out, not_2_out, not_3_out, or_1_out, or_2_out;

  not not_1 (not_1_out, X0);
  not not_2 (not_2_out, X1);
  not not_3 (not_3_out, S);
  and and_1 (and_1_out, X0, not_3_out);
  and and_2 (and_2_out, X1, S);
  or or_1 (or_1_out, X0, S);
  or or_2 (or_2_out, X1, not_3_out);
  or or_3 (Problem_7__Z__eq__m, and_1_out, and_2_out);
  and and_3 (Problem_8__Z__eq__M, or_1_out, or_2_out);
endmodule
