// Digital circuit 04-01.dig as structural Verilog
module _04_01 (
  input  [3:0] In,
  input  [1:0] Selector,
  output [3:0] Output
);

  wire [3:0] _642_3_1_o, _2421_1_o, cyclic_1_p5, excess_3_1_p5;

  // excess_3 excess_3_1: pin names not known; wires that end beside it: In[3], In[2], In[1], In[0], excess_3_1_p5
  // cyclic cyclic_1: pin names not known; wires that end beside it: In[3], In[2], In[1], In[0], cyclic_1_p5
  _2421 _2421_1 (.A(In[3]), .B(In[2]), .C(In[1]), .D(In[0]), .O(_2421_1_o));
  _642_3 _642_3_1 (.A(In[3]), .B(In[2]), .C(In[1]), .D(In[0]), .O(_642_3_1_o));
  Multiplexer #(.Bits(4), .Selector_Bits(2)) multiplexer_1 (
    .sel(Selector), .in_0(excess_3_1_p5), .in_1(cyclic_1_p5), .in_2(_2421_1_o), .in_3(_642_3_1_o),
    .out(Output));
endmodule
