// Digital circuit 04-02.dig as structural Verilog
module _04_02 (
  input  [6:0] In,
  output [6:0] Output
);

  wire h_a_1_p2, h_b_1_p2;

  // H_A h_a_1: pin names not known; wires that end beside it: In, h_a_1_p2
  // H_B h_b_1: pin names not known; wires that end beside it: h_a_1_p2, h_b_1_p2
  // H_C h_c_1: pin names not known; wires that end beside it: h_b_1_p2, In, Output
endmodule
