// Digital circuit H-A.dig as structural Verilog
module H_A (
  input  [6:0] H,
  output [2:0] O
);

  xor xor_1 (O[2], H[3], H[2], H[1], H[0]);
  xor xor_2 (O[1], H[5], H[4], H[1], H[0]);
  xor xor_3 (O[0], H[6], H[4], H[2], H[0]);
  // Pins of 1 and 3 bits meet at O
endmodule
