// Digital circuit H-B.dig as structural Verilog
module H_B (
  input  [2:0] C,
  output [6:0] P
);

  wire not_1_out, not_2_out, not_3_out;

  not not_1 (not_1_out, C[2]);
  not not_2 (not_2_out, C[1]);
  not not_3 (not_3_out, C[0]);
  and and_1 (P[6], not_1_out, not_2_out, C[0]);
  and and_2 (P[5], not_1_out, C[1], not_3_out);
  and and_3 (P[4], not_1_out, C[1], C[0]);
  and and_4 (P[3], C[2], not_2_out, not_3_out);
  and and_5 (P[2], C[2], not_2_out, C[0]);
  and and_6 (P[1], C[2], C[1], not_3_out);
  and and_7 (P[0], C[2], C[1], C[0]);
  // Pins of 1 and 7 bits meet at P
endmodule
