// Digital circuit cyclic.dig as structural Verilog
module cyclic (
  input  A,
  input  B,
  input  C,
  input  D,
  output [3:0] O
);

  wire and_1_out, and_2_out, and_3_out, and_4_out, not_1_out, not_2_out, not_3_out, not_4_out;

  not not_1 (not_1_out, A);
  not not_2 (not_2_out, B);
  not not_3 (not_3_out, C);
  not not_4 (not_4_out, D);
  and and_1 (and_1_out, B, not_3_out);
  and and_2 (and_2_out, not_2_out, C);
  and and_3 (and_3_out, C, not_4_out);
  and and_4 (and_4_out, not_3_out, D);
  or or_1 (O[2], A, B);
  or or_2 (O[1], and_1_out, and_2_out);
  or or_3 (O[0], and_3_out, and_4_out);
  // Pins of 1 and 4 bits meet at {A, O[2:0]}

  assign O[3] = A;
endmodule
