// Digital circuit excess-3.dig as structural Verilog
module excess_3 (
  input  A,
  input  B,
  input  C,
  input  D,
  output [3:0] O
);

  wire and_1_out, and_2_out, and_3_out, and_4_out, and_5_out, and_6_out, and_7_out, not_1_out, not_2_out,
       not_3_out;

  not not_1 (not_1_out, A);
  not not_2 (not_2_out, B);
  not not_3 (not_3_out, C);
  not not_4 (O[0], D);
  and and_1 (and_1_out, B, C);
  and and_2 (and_2_out, B, D);
  and and_3 (and_3_out, not_2_out, D);
  and and_4 (and_4_out, not_2_out, C);
  and and_5 (and_5_out, B, not_3_out, O[0]);
  and and_6 (and_6_out, not_3_out, O[0]);
  and and_7 (and_7_out, C, D);
  or or_1 (O[3], A, and_1_out, and_2_out);
  or or_2 (O[2], and_3_out, and_4_out, and_5_out);
  or or_3 (O[1], and_6_out, and_7_out);
  // Pins of 1 and 4 bits meet at O
endmodule
