// Digital circuit 05-02.dig as structural Verilog
module _05_02 (
  input  B,
  input  C,
  input  D,
  input  E,
  input  F,
  input  A,
  output Before,
  output After
);

  wire and_1_out, and_2_out, and_3_out, and_4_out, and_5_out, not_1_out, not_2_out, not_3_out, not_4_out,
       not_5_out, not_6_out;

  not not_1 (not_1_out, B);
  not not_2 (not_2_out, C);
  not not_3 (not_3_out, D);
  not not_4 (not_4_out, E);
  not not_5 (not_5_out, E);
  not not_6 (not_6_out, F);
  and and_1 (and_1_out, not_1_out, E, F);
  and and_2 (and_2_out, not_2_out, not_3_out, not_4_out);
  and and_3 (and_3_out, D, not_5_out, not_6_out);
  and and_4 (and_4_out, ~C, ~E, ~F);  // And
  and and_5 (and_5_out, ~B, ~C, ~D, F);  // And
  or or_1 (Before, and_1_out, and_2_out, and_3_out);
  or or_2 (After, and_1_out, and_2_out, and_3_out, and_4_out, and_5_out);
endmodule

/* Test case:
B C D E F Before After
1 0 0 0 0 1 1
1 0 1 0 0 1 1
1 0 0 0 0 1 1
1 0 1 0 0 1 1
1 0 0 0 0 1 1
1 0 1 0 0 1 1
0 0 0 0 0 1 1
0 0 1 0 0 1 1
0 0 0 0 0 1 1
0 0 1 0 0 1 1
0 0 0 0 0 1 1
0 0 0 0 1 1 1
0 0 0 1 1 1 1
0 0 0 0 1 1 1
0 0 0 1 1 1 1
0 0 0 0 1 1 1
0 0 0 1 1 1 1
0 0 0 0 1 1 1
*/
