// Digital circuit 05-03.dig as structural Verilog
module _05_03 (
  input  [7:0] In,
  output [8:0] Output
);

  wire halfadder_1_co, halfadder_2_co, halfadder_3_co, halfadder_4_co, halfadder_5_co, halfadder_6_co,
       halfadder_7_co, halfadder_8_co, halfadder_9_co, not_1_out, not_2_out, not_3_out, not_4_out, not_5_out,
       not_6_out, not_7_out, not_8_out;

  not not_1 (not_1_out, In[7]);
  not not_2 (not_2_out, In[6]);
  not not_3 (not_3_out, In[5]);
  not not_4 (not_4_out, In[4]);
  not not_5 (not_5_out, In[3]);
  not not_6 (not_6_out, In[2]);
  not not_7 (not_7_out, In[1]);
  not not_8 (not_8_out, In[0]);
  halfAdder halfadder_1 (.A(1'b1), .CI(halfadder_2_co), .S(Output[8]), .CO(halfadder_1_co));
  halfAdder halfadder_2 (.A(not_1_out), .CI(halfadder_3_co), .S(Output[7]), .CO(halfadder_2_co));
  halfAdder halfadder_3 (.A(not_2_out), .CI(halfadder_4_co), .S(Output[6]), .CO(halfadder_3_co));
  halfAdder halfadder_4 (.A(not_3_out), .CI(halfadder_5_co), .S(Output[5]), .CO(halfadder_4_co));
  halfAdder halfadder_5 (.A(not_4_out), .CI(halfadder_6_co), .S(Output[4]), .CO(halfadder_5_co));
  halfAdder halfadder_6 (.A(not_5_out), .CI(halfadder_7_co), .S(Output[3]), .CO(halfadder_6_co));
  halfAdder halfadder_7 (.A(not_6_out), .CI(halfadder_8_co), .S(Output[2]), .CO(halfadder_7_co));
  halfAdder halfadder_8 (.A(not_7_out), .CI(halfadder_9_co), .S(Output[1]), .CO(halfadder_8_co));
  halfAdder halfadder_9 (.A(not_8_out), .CI(1'b1), .S(Output[0]), .CO(halfadder_9_co));
  PullDown pulldown_1 (.out(halfadder_1_co));
endmodule
