// Digital circuit 05-04.dig as structural Verilog
module _05_04 (
  input  [3:0] In,
  output [3:0] Output
);

  wire halfadder_1_co, halfadder_2_co, halfadder_3_co, not_1_out, not_2_out, not_3_out, or_1_out;
  wire [2:0] halfadder_1_s;

  or or_1 (or_1_out, In[0], In[1], In[2]);
  not not_1 (not_1_out, In[2]);
  not not_2 (not_2_out, In[1]);
  not not_3 (not_3_out, In[0]);
  and and_1 (Output[3], or_1_out, In[3]);
  halfAdder halfadder_1 (.A(not_1_out), .CI(halfadder_2_co), .S(halfadder_1_s[2]), .CO(halfadder_1_co));
  halfAdder halfadder_2 (.A(not_2_out), .CI(halfadder_3_co), .S(halfadder_1_s[1]), .CO(halfadder_2_co));
  halfAdder halfadder_3 (.A(not_3_out), .CI(1'b1), .S(halfadder_1_s[0]), .CO(halfadder_3_co));
  Multiplexer #(.Bits(3)) multiplexer_1 (.sel(In[3]), .in_0(In[2:0]), .in_1(halfadder_1_s), .out(Output[2:0]));
  PullDown pulldown_1 (.out(halfadder_1_co));
endmodule
