// Digital circuit 06-01.dig as structural Verilog
module _06_01 (
  input  [3:0] A,
  input  [3:0] B,
  input  [2:0] S,
  input  M,
  input  C,
  output [3:0] F
);

  wire [3:0] arithmetic_1_o, logical_1_o;

  logical logical_1 (.A(A), .B(B), .S(S), .O(logical_1_o));
  arithmetic arithmetic_1 (.A(A), .B(B), .S(S), .C(C), .O(arithmetic_1_o));
  Multiplexer #(.Bits(4)) multiplexer_1 (.sel(M), .in_0(logical_1_o), .in_1(arithmetic_1_o), .out(F));
endmodule
