// Digital circuit arithmetic.dig as structural Verilog
module arithmetic (
  input  [3:0] A,
  input  [3:0] B,
  input  [2:0] S,
  input  C,
  output [3:0] O
);

  wire add_1_c_o, add_2_c_o, add_3_c_o, add_4_c_o, add_5_c_o, add_6_c_o;
  wire [3:0] add_1_s, add_2_s, add_3_s, add_4_s, add_5_s, add_6_s, multiplexer_1_out, not_1_out, not_2_out;

  Multiplexer #(.Bits(4)) multiplexer_1 (.sel(C), .in_0(4'b1111), .in_1(4'b0000), .out(multiplexer_1_out));
  assign not_1_out = ~B;  // Not not_1, 4 bits wide
  assign not_2_out = ~A;  // Not not_2, 4 bits wide
  Add #(.Bits(4)) add_1 (.a(A), .b(4'b0000), .c_i(C), .s(add_1_s), .c_o(add_1_c_o));
  Add #(.Bits(4)) add_2 (.a(A), .b(multiplexer_1_out), .c_i(1'b0), .s(add_2_s), .c_o(add_2_c_o));
  Add #(.Bits(4)) add_3 (.a(A), .b(B), .c_i(C), .s(add_3_s), .c_o(add_3_c_o));
  Add #(.Bits(4)) add_4 (.a(A), .b(not_1_out), .c_i(C), .s(add_4_s), .c_o(add_4_c_o));
  Add #(.Bits(4)) add_5 (.a(not_2_out), .b(4'b0000), .c_i(C), .s(add_5_s), .c_o(add_5_c_o));
  Add #(.Bits(4)) add_6 (.a(B), .b(4'b0000), .c_i(C), .s(add_6_s), .c_o(add_6_c_o));
  PullDown pulldown_1 (.out(add_1_c_o));
  PullDown pulldown_2 (.out(add_2_c_o));
  PullDown pulldown_3 (.out(add_3_c_o));
  PullDown pulldown_4 (.out(add_4_c_o));
  PullDown pulldown_5 (.out(add_5_c_o));
  PullDown pulldown_6 (.out(add_6_c_o));
  Multiplexer #(.Bits(4), .Selector_Bits(3)) multiplexer_2 (
    .sel(S), .in_0(add_1_s), .in_1(add_2_s), .in_2(add_3_s), .in_3(add_4_s), .in_4(add_5_s), .in_5(add_6_s),
    .in_6({A[2:0], 1'b0}), .in_7({1'b0, A[3:1]}), .out(O));
endmodule
